// Logisim project mini_processor.circ as structural Verilog: 6 circuits, main circuit main
module FullAdder (
  input  A,
  input  B,
  input  Cin,
  output Sum,
  output Cout
);

  wire and_1_out, and_2_out, xor_1_out;

  xor xor_1 (xor_1_out, A, B);
  and and_1 (and_1_out, A, B);
  xor xor_2 (Sum, xor_1_out, Cin);
  and and_2 (and_2_out, xor_1_out, Cin);
  or or_1 (Cout, and_1_out, and_2_out);
endmodule

module AdderSubtractor4Bit (
  input  [3:0] A,
  input  [3:0] B,
  input  Sub,
  output [3:0] Result,
  output Cout
);

  wire [3:0] xor_1_out;
  wire [3:1] bit_extender_1_out;

  assign xor_1_out = B ^ {bit_extender_1_out, Sub};  // XOR_Gate xor_1, 4 bits wide
  Bit_Extender #(.in_width(1), .out_width(4)) bit_extender_1 (.out({bit_extender_1_out, Sub}));  // open: in
  Adder #(.width(4)) adder_1 (.a(A), .b(xor_1_out), .out(Result), .cout(Sub));  // open: cin
  // Pins of 1 and 4 bits meet at {bit_extender_1_out, Sub}
endmodule

module Decoder3to8 (
  input  [2:0] Opcode,
  output D0_AND,
  output D1_OR,
  output D2_XOR,
  output D3_ADD,
  output D4_SUB,
  output D5_UNUSED,
  output D6_UNUSED,
  output D7_UNUSED
);

  // Decoder #(.select(3)) decoder_1: pin names not known; wires that end beside it: Opcode, D0_AND, D1_OR, D2_XOR, D3_ADD, D4_SUB, D5_UNUSED, D6_UNUSED, D7_UNUSED
endmodule

module ControlUnit (
  input  [2:0] Opcode,
  output [2:0] ALU_Sel,
  output RegWrite,
  output SubSignal
);

  wire decoder3to8_1_p1, decoder3to8_1_p2, decoder3to8_1_p3, decoder3to8_1_p4;

  // Decoder3to8 decoder3to8_1: pin names not known; wires that end beside it: decoder3to8_1_p1, decoder3to8_1_p2, decoder3to8_1_p3, decoder3to8_1_p4, SubSignal
  // OR_Gate or_1: pin names not known; wires that end beside it: SubSignal, decoder3to8_1_p2, decoder3to8_1_p4, decoder3to8_1_p1, decoder3to8_1_p3, RegWrite

  assign ALU_Sel = Opcode;
endmodule

module ALU4Bit (
  input  [3:0] A,
  input  [3:0] B,
  input  [2:0] ALU_Sel,
  output [3:0] Result,
  output Zero,
  output Cout
);

  wire addersubtractor4bit_1_p3;
  wire [3:0] and_1_out, or_1_out, xor_1_out;

  assign and_1_out = A & B;  // AND_Gate and_1, 4 bits wide
  assign or_1_out = A | B;  // OR_Gate or_1, 4 bits wide
  assign xor_1_out = A ^ B;  // XOR_Gate xor_1, 4 bits wide
  // AdderSubtractor4Bit addersubtractor4bit_1: pin names not known; wires that end beside it: A, B, addersubtractor4bit_1_p3, Cout
  // Multiplexer #(.select(3), .width(4)) multiplexer_1: pin names not known; wires that end beside it: and_1_out, or_1_out, xor_1_out, addersubtractor4bit_1_p3, addersubtractor4bit_1_p3, ALU_Sel, Result
  // NOR_Gate nor_1: pin names not known; wires that end beside it: Result[0], Zero
endmodule

module main (
  input  [3:0] Input_A,
  input  [3:0] Input_B,
  input  [2:0] Opcode,
  input  Load_A,
  input  Load_B,
  output [3:0] Final_Output,
  output Zero_Flag,
  output Carry_Flag
);

  wire Clock_out, controlunit_1_regwrite;
  wire [2:0] controlunit_1_alu_sel;
  wire [3:0] alu4bit_1_p4, register_1_q, register_2_q;

  Clock Clock (.out(Clock_out));
  Register #(.width(4)) register_1 (.D(Input_A), .en(Load_A), .clk(Clock_out), .Q(register_1_q));  // open: clr
  Register #(.width(4)) register_2 (.D(Input_B), .en(Load_B), .clk(Clock_out), .Q(register_2_q));  // open: clr
  ControlUnit controlunit_1 (
    .ALU_Sel(controlunit_1_alu_sel), .RegWrite(controlunit_1_regwrite));  // open: Opcode, SubSignal
  // ALU4Bit alu4bit_1: pin names not known; wires that end beside it: register_1_q, register_2_q, controlunit_1_alu_sel, alu4bit_1_p4, Zero_Flag, Carry_Flag
  Register #(.width(4)) register_3 (
    .D(alu4bit_1_p4), .en(controlunit_1_regwrite), .clk(Clock_out), .Q(Final_Output));  // open: clr
endmodule
